# Fritzing sketch DotMatrix Fritzing (saved by Fritzing 0.9.3b)
breadboards: 2

parts:
  JP1 = Header 8 [package=1x08_smd]
  JP2 = Header 8 [package=1x08_smd]
  JP3 = Header 8 [package=1x08_smd]
  JP4 = Header 8 [package=1x08_smd]
  R1 = Resistor [tolerance=±5% resistance=220 package=THT]
  R2 = Resistor [tolerance=±5% resistance=220 package=THT]
  R3 = Resistor [tolerance=±5% resistance=220 package=THT]
  R4 = Resistor [tolerance=±5% resistance=220 package=THT]
  R5 = Resistor [tolerance=±5% resistance=220 package=THT]
  R6 = Resistor [tolerance=±5% resistance=220 package=THT]
  R7 = Resistor [tolerance=±5% resistance=220 package=THT]
  R8 = Resistor [tolerance=±5% resistance=220 package=THT]

nets:
  N1: JP1.1, R6.Pin_0
  N2: JP1.4, R7.Pin_0
  N3: JP1.7, R8.Pin_0
  N4: JP2.1, R1.Pin_0
  N5: JP2.2, R2.Pin_0
  N6: JP2.5, R5.Pin_0
  N7: JP2.7, R3.Pin_0
  N8: JP2.8, R4.Pin_0
  N9: JP3.2, R8.Pin_1
  N10: JP3.5, R7.Pin_1
  N11: JP3.8, R6.Pin_1
  N12: JP4.1, R1.Pin_1
  N13: JP4.2, R2.Pin_1
  N14: JP4.5, R5.Pin_1
  N15: JP4.7, R3.Pin_1
  N16: JP4.8, R4.Pin_1

notes:
  dot matrix
  red: row
  blue:col
